// Logisim project 12bit_shift_reg.circ as structural Verilog: 1 circuit, main circuit main
module main (
  input  i_p,
  input  rst,
  input  En,
  output out_4,
  output out_5,
  output out_6,
  output out_7,
  output out_8,
  output out_9,
  output out_10,
  output out_11,
  output out_12,
  output out_13,
  output out_14,
  output out_15,
  output out_16,
  output out_17,
  output out_18,
  output out_19
);

  wire clock_1_out, d_ff_1_q, d_ff_2_q, d_ff_4_q, d_ff_6_q, d_ff_8_q, d_ff_10_q, d_ff_12_q, d_ff_14_q,
       d_ff_16_q, d_ff_19_q, d_ff_20_q, d_ff_22_q, mod12_counter_1_f_12;

  Clock clock_1 (.out(clock_1_out));
  D_Flip_Flop d_ff_1 (.clk(clock_1_out), .D(i_p), .Q(d_ff_1_q));  // open: Qn, preset, en, reset
  mod12_counter mod12_counter_1 (
    .clk(clock_1_out), .En(En), .reset(rst), .f_12(mod12_counter_1_f_12));  // open: q3_msb, q2, q1, q0_lsb
  D_Flip_Flop d_ff_2 (.clk(clock_1_out), .D(d_ff_1_q), .Q(d_ff_2_q));  // open: Qn, preset, en, reset
  D_Flip_Flop d_ff_3 (.clk(mod12_counter_1_f_12), .D(d_ff_1_q), .Q(out_4));  // open: Qn, preset, en, reset
  D_Flip_Flop d_ff_4 (.clk(clock_1_out), .D(d_ff_2_q), .Q(d_ff_4_q));  // open: Qn, preset, en, reset
  D_Flip_Flop d_ff_5 (.clk(mod12_counter_1_f_12), .D(d_ff_2_q), .Q(out_5));  // open: Qn, preset, en, reset
  D_Flip_Flop d_ff_6 (.clk(clock_1_out), .D(d_ff_4_q), .Q(d_ff_6_q));  // open: Qn, preset, en, reset
  D_Flip_Flop d_ff_7 (.clk(mod12_counter_1_f_12), .D(d_ff_4_q), .Q(out_6));  // open: Qn, preset, en, reset
  D_Flip_Flop d_ff_8 (.clk(clock_1_out), .D(d_ff_6_q), .Q(d_ff_8_q));  // open: Qn, preset, en, reset
  D_Flip_Flop d_ff_9 (.clk(mod12_counter_1_f_12), .D(d_ff_6_q), .Q(out_7));  // open: Qn, preset, en, reset
  D_Flip_Flop d_ff_10 (.clk(clock_1_out), .D(d_ff_8_q), .Q(d_ff_10_q));  // open: Qn, preset, en, reset
  D_Flip_Flop d_ff_11 (.clk(mod12_counter_1_f_12), .D(d_ff_8_q), .Q(out_8));  // open: Qn, preset, en, reset
  D_Flip_Flop d_ff_12 (.clk(clock_1_out), .D(d_ff_10_q), .Q(d_ff_12_q));  // open: Qn, preset, en, reset
  D_Flip_Flop d_ff_13 (.clk(mod12_counter_1_f_12), .D(d_ff_10_q), .Q(out_9));  // open: Qn, preset, en, reset
  back_prop back_prop_1 (
    .RST(rst), .clk(clock_1_out), .En(En), .C10(out_5), .C11(out_4), .C8(out_7), .C9(out_6), .C6(out_9),
    .C7(out_8), .C4(out_11), .C5(out_10), .C2(out_13), .C3(out_12), .C0(out_15), .C1(out_14), .M0(out_16),
    .M1(out_17), .M2(out_18), .M3(out_19));
  D_Flip_Flop d_ff_14 (.clk(clock_1_out), .D(d_ff_12_q), .Q(d_ff_14_q));  // open: Qn, preset, en, reset
  D_Flip_Flop d_ff_15 (.clk(mod12_counter_1_f_12), .D(d_ff_12_q), .Q(out_10));  // open: Qn, preset, en, reset
  D_Flip_Flop d_ff_16 (.clk(clock_1_out), .D(d_ff_14_q), .Q(d_ff_16_q));  // open: Qn, preset, en, reset
  D_Flip_Flop d_ff_17 (.clk(mod12_counter_1_f_12), .D(d_ff_14_q), .Q(out_11));  // open: Qn, preset, en, reset
  D_Flip_Flop d_ff_18 (.clk(mod12_counter_1_f_12), .D(d_ff_16_q), .Q(out_12));  // open: Qn, preset, en, reset
  D_Flip_Flop d_ff_19 (.clk(clock_1_out), .D(d_ff_16_q), .Q(d_ff_19_q));  // open: Qn, preset, en, reset
  D_Flip_Flop d_ff_20 (.clk(clock_1_out), .D(d_ff_19_q), .Q(d_ff_20_q));  // open: Qn, preset, en, reset
  D_Flip_Flop d_ff_21 (.clk(mod12_counter_1_f_12), .D(d_ff_19_q), .Q(out_13));  // open: Qn, preset, en, reset
  D_Flip_Flop d_ff_22 (.clk(clock_1_out), .D(d_ff_20_q), .Q(d_ff_22_q));  // open: Qn, preset, en, reset
  D_Flip_Flop d_ff_23 (.clk(mod12_counter_1_f_12), .D(d_ff_20_q), .Q(out_14));  // open: Qn, preset, en, reset
  D_Flip_Flop d_ff_24 (.clk(mod12_counter_1_f_12), .D(d_ff_22_q), .Q(out_15));  // open: Qn, preset, en, reset

  // Notes on the sheet:
  //   required libraries:
  //   f/12 clock , back_propagation
endmodule
