// Logisim project 4_to1_mux.circ as structural Verilog: 1 circuit, main circuit 4:1mux
module _4_1mux (
  input  I0,
  input  I1,
  input  I2,
  input  I3,
  input  S0,
  input  S1,
  input  En,
  output mux_out
);

  wire multiplexer_1_out, multiplexer_2_out;

  Multiplexer multiplexer_1 (.in0(I0), .in1(I1), .out(multiplexer_1_out), .sel(S0), .en(En));
  Multiplexer multiplexer_2 (.in0(I2), .in1(I3), .out(multiplexer_2_out), .sel(S0), .en(En));
  Multiplexer multiplexer_3 (.in0(multiplexer_1_out), .in1(multiplexer_2_out), .out(mux_out), .sel(S1), .en(En));
endmodule
