// Logisim project 8bit_reg S3.circ as structural Verilog: 1 circuit, main circuit 8bit_reg S3
module _8bit_reg_S3 (
  input  clk,
  input  b0,
  input  b1,
  input  b2,
  input  b3,
  input  pb0,
  input  pb1,
  input  RST,
  output b0_2,
  output b1_2,
  output b2_2,
  output b3_2,
  output pb0_2,
  output pb1_2,
  output sb0,
  output sb1
);

  D_Flip_Flop d_ff_1 (.clk(clk), .D(b0), .Q(b0_2), .reset(RST));  // open: Qn, preset, en
  D_Flip_Flop d_ff_2 (.clk(clk), .D(b1), .Q(b1_2), .reset(RST));  // open: Qn, preset, en
  D_Flip_Flop d_ff_3 (.clk(clk), .D(b2), .Q(b2_2), .reset(RST));  // open: Qn, preset, en
  D_Flip_Flop d_ff_4 (.clk(clk), .D(b3), .Q(b3_2), .reset(RST));  // open: Qn, preset, en
  D_Flip_Flop d_ff_5 (.clk(clk), .D(pb0), .Q(pb0_2), .reset(RST));  // open: Qn, preset, en
  D_Flip_Flop d_ff_6 (.clk(clk), .D(pb1), .Q(pb1_2), .reset(RST));  // open: Qn, preset, en
  D_Flip_Flop d_ff_7 (.clk(clk), .D(1'b1), .Q(sb0), .preset(1'b1));  // open: Qn, en, reset
  D_Flip_Flop d_ff_8 (.clk(clk), .D(1'b1), .Q(sb1), .preset(1'b1));  // open: Qn, en, reset
endmodule
