// Logisim project Hamming+adder.circ as structural Verilog: 1 circuit, main circuit Hamming+adder
module Hamming_adder (
  input  B00,
  input  EXT,
  input  B01,
  input  B02,
  input  B03,
  input  CIN0,
  input  IN00,
  input  CIN1,
  input  IN01,
  input  B10,
  input  B11,
  input  B12,
  input  B13,
  input  IN10,
  input  IN11,
  output S00,
  output S01,
  output S02,
  output S03,
  output S10,
  output S11,
  output S12,
  output S13
);

  wire hamming_1_lsb, hamming_1_msb, hamming_2_lsb, hamming_2_msb;

  HAMMING hamming_1 (.CIN0(CIN0), .IN0(IN10), .CIN1(CIN1), .IN1(IN11), .LSB(hamming_1_lsb), .MSB(hamming_1_msb));
  HAMMING hamming_2 (.CIN0(CIN0), .IN0(IN00), .CIN1(CIN1), .IN1(IN01), .LSB(hamming_2_lsb), .MSB(hamming_2_msb));
  _4B_ADDER u_4b_adder_1 (
    .B0(B00), .EXT(EXT), .B1(B01), .B2(B02), .B3(B03), .C0(hamming_2_lsb), .C1(hamming_2_msb), .S0(S00),
    .S1(S01), .S2(S02), .S3(S03));
  _4B_ADDER u_4b_adder_2 (
    .B0(B10), .EXT(EXT), .B1(B11), .B2(B12), .B3(B13), .C0(hamming_1_lsb), .C1(hamming_1_msb), .S0(S10),
    .S1(S11), .S2(S12), .S3(S13));

  // Notes on the sheet:
  //   expected bits
  //   input bits
  //   present discrepancy
  //   should include library viterbi.circ
endmodule
