// Logisim project VITERBI.circ as structural Verilog
module _1b_FA (
  input  A,
  input  B,
  input  CIN,
  output SUM,
  output COUT
);

  wire and_1_out, and_2_out, and_3_out;

  xor xor_1 (SUM, A, B, CIN);
  and and_1 (and_1_out, A, B);
  and and_2 (and_2_out, CIN, B);
  and and_3 (and_3_out, A, CIN);
  or or_1 (COUT, and_1_out, and_2_out, and_3_out);
endmodule

module _4B_ADDER (
  input  B0,
  input  EXT,
  input  B1,
  input  B2,
  input  B3,
  input  C0,
  input  C1,
  output S0,
  output S1,
  output S2,
  output S3
);

  wire n1b_fa_1_cout, n1b_fa_2_cout, n1b_fa_3_cout;

  _1b_FA u_1b_fa_1 (.A(B0), .B(C0), .CIN(EXT), .SUM(S0), .COUT(n1b_fa_1_cout));
  _1b_FA u_1b_fa_2 (.A(B1), .B(C1), .CIN(n1b_fa_1_cout), .SUM(S1), .COUT(n1b_fa_2_cout));
  _1b_FA u_1b_fa_3 (.A(B2), .B(EXT), .CIN(n1b_fa_2_cout), .SUM(S2), .COUT(n1b_fa_3_cout));
  _1b_FA u_1b_fa_4 (.A(B3), .B(EXT), .CIN(n1b_fa_3_cout), .SUM(S3));  // open: COUT
endmodule

module HAMMING (
  input  CIN0,
  input  IN0,
  input  CIN1,
  input  IN1,
  output LSB,
  output MSB
);

  wire xor_1_out, xor_2_out;

  xor xor_1 (xor_1_out, CIN0, IN0);
  xor xor_2 (xor_2_out, CIN1, IN1);
  xor xor_3 (LSB, xor_1_out, xor_2_out);
  and and_1 (MSB, xor_2_out, xor_1_out);
endmodule
