// Logisim project back_prop.circ as structural Verilog: 1 circuit, main circuit back_prop
module back_prop (
  input  RST,
  input  clk,
  input  C3,
  input  C0,
  input  C5,
  input  C2,
  input  C10,
  input  C11,
  input  C8,
  input  C9,
  input  C6,
  input  C7,
  input  C4,
  input  C1,
  input  En,
  output M0,
  output M1,
  output M2,
  output M3
);

  wire main_1_c1r1_0, main_1_c1r1_1, main_1_c1r2_0, main_1_c1r2_1, main_1_c2r1_0, main_1_c2r1_1,
       main_1_c2r2_0, main_1_c2r2_1, main_1_c2r3_0, main_1_c2r3_1, main_1_c2r4_0, main_1_c2r4_1,
       main_1_c3r1_0, main_1_c3r1_1, main_1_c3r2_0, main_1_c3r2_1, main_1_c3r3_0, main_1_c3r3_1,
       main_1_c3r4_0, main_1_c3r4_1, main_1_c4r1_0, main_1_c4r1_1, main_1_c4r2_0, main_1_c4r2_1,
       main_1_c4r3_0, main_1_c4r3_1, main_1_c4r4_0, main_1_c4r4_1, main_1_c5r1_0, main_1_c5r1_1,
       main_1_c5r2_0, main_1_c5r2_1, main_1_c5r3_0, main_1_c5r3_1, main_1_c5r4_0, main_1_c5r4_1, main_1_l0,
       main_1_l1, n4_1mux_1_mux_out, n4_1mux_2_mux_out, n4_1mux_4_mux_out, n4_1mux_6_mux_out,
       n4_1mux_8_mux_out;

  trellis_path_main main_1 (
    .CLK(clk), .L1(main_1_l1), .L0(main_1_l0), .RSET(RST), .C11(C11), .C10(C10), .C1R1_0(main_1_c1r1_0),
    .C1R2_0(main_1_c1r2_0), .C1R1_1(main_1_c1r1_1), .C1R2_1(main_1_c1r2_1), .C9(C9), .C8(C8),
    .C2R1_0(main_1_c2r1_0), .C2R2_0(main_1_c2r2_0), .C2R3_0(main_1_c2r3_0), .C2R4_0(main_1_c2r4_0),
    .C2R2_1(main_1_c2r2_1), .C2R3_1(main_1_c2r3_1), .C2R4_1(main_1_c2r4_1), .C2R1_1(main_1_c2r1_1), .C7(C7),
    .C6(C6), .C3R2_0(main_1_c3r2_0), .C3R3_0(main_1_c3r3_0), .C3R4_0(main_1_c3r4_0), .C3R2_1(main_1_c3r2_1),
    .C3R3_1(main_1_c3r3_1), .C3R4_1(main_1_c3r4_1), .C3R1_0(main_1_c3r1_0), .C3R1_1(main_1_c3r1_1), .C5(C5),
    .C4(C4), .C4R2_0(main_1_c4r2_0), .C4R3_0(main_1_c4r3_0), .C4R4_0(main_1_c4r4_0), .C4R1_0(main_1_c4r1_0),
    .C4R2_1(main_1_c4r2_1), .C4R3_1(main_1_c4r3_1), .C4R4_1(main_1_c4r4_1), .C4R1_1(main_1_c4r1_1), .C3(C3),
    .C2(C2), .C5R1_0(main_1_c5r1_0), .C5R2_0(main_1_c5r2_0), .C5R3_0(main_1_c5r3_0), .C5R4_0(main_1_c5r4_0),
    .C5R2_1(main_1_c5r2_1), .C5R3_1(main_1_c5r3_1), .C5R4_1(main_1_c5r4_1), .C5R1_1(main_1_c5r1_1), .C1(C1),
    .C0(C0));
  _4_1mux u_4_1mux_1 (
    .I0(main_1_c5r1_0), .I1(main_1_c5r2_0), .I2(main_1_c5r3_0), .I3(main_1_c5r4_0), .S0(main_1_l0),
    .S1(main_1_l1), .En(En), .mux_out(n4_1mux_1_mux_out));
  _4_1mux u_4_1mux_2 (
    .I0(main_1_c5r1_1), .I1(main_1_c5r2_1), .I2(main_1_c5r3_1), .I3(main_1_c5r4_1), .S0(main_1_l0),
    .S1(main_1_l1), .En(En), .mux_out(n4_1mux_2_mux_out));
  _4_1mux u_4_1mux_3 (
    .I0(main_1_c4r1_0), .I1(main_1_c4r2_0), .I2(main_1_c4r3_0), .I3(main_1_c4r4_0), .S0(n4_1mux_1_mux_out),
    .S1(n4_1mux_2_mux_out), .En(En), .mux_out(M0));
  _4_1mux u_4_1mux_4 (
    .I0(main_1_c4r1_1), .I1(main_1_c4r2_1), .I2(main_1_c4r3_1), .I3(main_1_c4r4_1), .S0(n4_1mux_1_mux_out),
    .S1(n4_1mux_2_mux_out), .En(En), .mux_out(n4_1mux_4_mux_out));
  _4_1mux u_4_1mux_5 (
    .I0(main_1_c3r1_0), .I1(main_1_c3r2_0), .I2(main_1_c3r3_0), .I3(main_1_c3r4_0), .S0(M0),
    .S1(n4_1mux_4_mux_out), .En(En), .mux_out(M1));
  _4_1mux u_4_1mux_6 (
    .I0(main_1_c3r1_1), .I1(main_1_c3r2_1), .I2(main_1_c3r3_1), .I3(main_1_c3r4_1), .S0(M0),
    .S1(n4_1mux_4_mux_out), .En(En), .mux_out(n4_1mux_6_mux_out));
  _4_1mux u_4_1mux_7 (
    .I0(main_1_c2r1_0), .I1(main_1_c2r2_0), .I2(main_1_c2r3_0), .I3(main_1_c2r4_0), .S0(M1),
    .S1(n4_1mux_6_mux_out), .En(En), .mux_out(M2));
  _4_1mux u_4_1mux_8 (
    .I0(main_1_c2r1_1), .I1(main_1_c2r2_1), .I2(main_1_c2r3_1), .I3(main_1_c2r4_1), .S0(M1),
    .S1(n4_1mux_6_mux_out), .En(En), .mux_out(n4_1mux_8_mux_out));
  _4_1mux u_4_1mux_9 (
    .I0(main_1_c1r1_0), .I1(main_1_c1r2_0), .S0(M2), .S1(n4_1mux_8_mux_out), .En(En), .mux_out(M3));  // open: I2, I3
  _4_1mux u_4_1mux_10 (
    .I0(main_1_c1r1_1), .I1(main_1_c1r2_1), .S0(M2), .S1(n4_1mux_8_mux_out), .En(En));  // open: I2, I3, mux_out

  // Notes on the sheet:
  //   required Librarires:     trellis_path , 4:1mux
endmodule
