// Logisim project encoder_and_noise.circ as structural Verilog: 1 circuit, main circuit encoder+noise
module encoder_noise (
  input  m3_msb,
  input  m2,
  input  m1,
  input  m0_lsb,
  input  clk,
  input  en,
  input  rst,
  output out_8
);

  wire encoder_1_enc_out, main_1_a_b, mod12_counter_1_f_12, mod12_counter_1_q0_lsb, mod12_counter_1_q1,
       mod12_counter_1_q2, mod12_counter_1_q3_msb, sequence_counter_1_q0_lsb, sequence_counter_1_q1,
       sequence_counter_1_q2, sequence_counter_1_q3_msb;

  encoder encoder_1 (
    .mo_lsb(m0_lsb), .m1(m1), .m2(m2), .m3_msb(m3_msb), .clk(clk), .En(en), .reset(rst),
    .enc_out(encoder_1_enc_out));
  mod12_counter mod12_counter_1 (
    .clk(clk), .En(en), .reset(rst), .f_12(mod12_counter_1_f_12), .q3_msb(mod12_counter_1_q3_msb),
    .q2(mod12_counter_1_q2), .q1(mod12_counter_1_q1), .q0_lsb(mod12_counter_1_q0_lsb));
  sequence_counter sequence_counter_1 (
    .clock(mod12_counter_1_f_12), .En(en), .Reset(rst), .q3_msb(sequence_counter_1_q3_msb),
    .q2(sequence_counter_1_q2), .q1(sequence_counter_1_q1), .q0_lsb(sequence_counter_1_q0_lsb));
  mag4_comp_main main_1 (
    .A3(mod12_counter_1_q3_msb), .A2(mod12_counter_1_q2), .A1(mod12_counter_1_q1),
    .A0(mod12_counter_1_q0_lsb), .B3(sequence_counter_1_q3_msb), .B2(sequence_counter_1_q2),
    .B1(sequence_counter_1_q1), .B0(sequence_counter_1_q0_lsb), .A_B(main_1_a_b));  // open: A_B_2, A_B_3
  xor xor_1 (out_8, main_1_a_b, encoder_1_enc_out);

  // Notes on the sheet:
  //   required libraries: mag4_comp,mod12_counter,my_encoder,seq_counter
endmodule
