// Logisim project hamming+add+comp.circ as structural Verilog: 1 circuit, main circuit hamming+add+comp
module hamming_add_comp (
  input  B00,
  input  EXT,
  input  B01,
  input  B02,
  input  B03,
  input  CIN0,
  input  IN00,
  input  CIN1,
  input  IN01,
  input  B10,
  input  B11,
  input  B12,
  input  B13,
  input  IN10,
  input  IN11,
  input  AS0,
  input  AS1,
  input  BS0,
  input  BS1,
  output S0_lsb,
  output S1,
  output S2,
  output S3_msb,
  output PB0,
  output PB1
);

  wire hamming_adder_1_s00, hamming_adder_1_s01, hamming_adder_1_s02, hamming_adder_1_s03,
       hamming_adder_1_s10, hamming_adder_1_s11, hamming_adder_1_s12, hamming_adder_1_s13, main_1_a_b,
       main_1_a_b_3, or_1_out;

  Hamming_adder hamming_adder_1 (
    .B00(B00), .EXT(EXT), .B01(B01), .B02(B02), .B03(B03), .CIN0(CIN0), .IN00(IN00), .CIN1(CIN1),
    .IN01(IN01), .B10(B10), .B11(B11), .B12(B12), .B13(B13), .IN10(IN10), .IN11(IN11),
    .S00(hamming_adder_1_s00), .S01(hamming_adder_1_s01), .S02(hamming_adder_1_s02),
    .S03(hamming_adder_1_s03), .S10(hamming_adder_1_s10), .S11(hamming_adder_1_s11),
    .S12(hamming_adder_1_s12), .S13(hamming_adder_1_s13));
  mag4_comp_main main_1 (
    .A3(hamming_adder_1_s03), .A2(hamming_adder_1_s02), .A1(hamming_adder_1_s01), .A0(hamming_adder_1_s00),
    .B3(hamming_adder_1_s13), .B2(hamming_adder_1_s12), .B1(hamming_adder_1_s11), .B0(hamming_adder_1_s10),
    .A_B(main_1_a_b), .A_B_3(main_1_a_b_3));  // open: A_B_2
  or or_1 (or_1_out, main_1_a_b, main_1_a_b_3);
  Multiplexer multiplexer_1 (
    .in0(hamming_adder_1_s00), .in1(hamming_adder_1_s10), .out(S0_lsb), .sel(or_1_out), .en(1'b1));
  Multiplexer multiplexer_2 (.in0(hamming_adder_1_s01), .in1(hamming_adder_1_s11), .out(S1), .sel(or_1_out), .en(1'b1));
  Multiplexer multiplexer_3 (.in0(hamming_adder_1_s02), .in1(hamming_adder_1_s12), .out(S2), .sel(or_1_out), .en(1'b1));
  Multiplexer multiplexer_4 (
    .in0(hamming_adder_1_s03), .in1(hamming_adder_1_s13), .out(S3_msb), .sel(or_1_out), .en(1'b1));
  Multiplexer multiplexer_5 (.in0(AS0), .in1(BS0), .out(PB0), .sel(or_1_out), .en(1'b1));
  Multiplexer multiplexer_6 (.in0(AS1), .in1(BS1), .out(PB1), .sel(or_1_out), .en(1'b1));

  // Notes on the sheet:
  //   required libraries: hamming+adder,mag4_comp
endmodule
