// Logisim project mag4_comp.circ as structural Verilog: 1 circuit, main circuit main
module main (
  input  A3,
  input  A2,
  input  A1,
  input  A0,
  input  B3,
  input  B2,
  input  B1,
  input  B0,
  output A_B,
  output A_B_2,
  output A_B_3
);

  wire and_2_out, and_3_out, and_4_out, and_5_out, not_1_out, not_2_out, not_3_out, not_4_out, xnor_1_out,
       xnor_2_out, xnor_3_out, xnor_4_out;

  xnor xnor_1 (xnor_1_out, A3, B3);
  xnor xnor_2 (xnor_2_out, A2, B2);
  xnor xnor_3 (xnor_3_out, A1, B1);
  xnor xnor_4 (xnor_4_out, A0, B0);
  not not_1 (not_1_out, B3);
  not not_2 (not_2_out, B2);
  not not_3 (not_3_out, B1);
  not not_4 (not_4_out, B0);
  and and_1 (A_B, xnor_1_out, xnor_2_out, xnor_3_out, xnor_4_out);
  and and_2 (and_2_out, xnor_3_out, xnor_2_out, xnor_1_out, not_4_out, A0);
  and and_3 (and_3_out, xnor_2_out, xnor_1_out, not_3_out, A1);
  and and_4 (and_4_out, xnor_1_out, not_2_out, A2);
  and and_5 (and_5_out, not_1_out, A3);
  or or_1 (A_B_3, and_2_out, and_3_out, and_4_out, and_5_out);
  nor nor_1 (A_B_2, A_B, A_B_3);

  // Notes on the sheet:
  //   a3
  //   a0
endmodule
