// Logisim project mod12_counter.circ as structural Verilog: 1 circuit, main circuit mod12_counter
module mod12_counter (
  input  clk,
  input  En,
  input  reset,
  output f_12,
  output q3_msb,
  output q2,
  output q1,
  output q0_lsb
);

  wire and_1_out, and_2_out, and_3_out, and_4_out, or_1_out;

  T_Flip_Flop t_ff_1 (.clk(clk), .T(En), .Q(q0_lsb), .reset(or_1_out), .en(En));  // open: Qn, preset
  T_Flip_Flop t_ff_2 (.clk(clk), .T(q0_lsb), .Q(q1), .reset(or_1_out), .en(En));  // open: Qn, preset
  and and_1 (and_1_out, q0_lsb, q1);
  T_Flip_Flop t_ff_3 (.clk(clk), .T(and_1_out), .Q(q2), .reset(or_1_out), .en(En));  // open: Qn, preset
  and and_2 (and_2_out, and_1_out, q2);
  T_Flip_Flop t_ff_4 (.clk(clk), .T(and_2_out), .Q(q3_msb), .reset(or_1_out), .en(En));  // open: Qn, preset
  or or_1 (or_1_out, and_4_out, reset);
  and and_3 (and_3_out, and_1_out, q3_msb);
  and and_4 (and_4_out, q2, q3_msb);
  D_Flip_Flop d_ff_1 (.clk(clk), .D(and_3_out), .Q(f_12), .en(En), .reset(reset));  // open: Qn, preset

  // Notes on the sheet:
  //              f/12_enable
  //   clear
endmodule
