// Logisim project mod_6_counter.circ as structural Verilog: 1 circuit, main circuit mod_6
module mod_6 (
  input  clk,
  input  En,
  input  reset,
  output Q2_msb,
  output Q1,
  output Qo_lsb
);

  wire and_1_out, and_2_out, or_1_out;

  T_Flip_Flop t_ff_1 (.clk(clk), .T(En), .Q(Qo_lsb), .reset(or_1_out), .en(En));  // open: Qn, preset
  T_Flip_Flop t_ff_2 (.clk(clk), .T(Qo_lsb), .Q(Q1), .reset(or_1_out), .en(En));  // open: Qn, preset
  and and_1 (and_1_out, Q1, Qo_lsb);
  T_Flip_Flop t_ff_3 (.clk(clk), .T(and_1_out), .Q(Q2_msb), .reset(or_1_out), .en(En));  // open: Qn, preset
  or or_1 (or_1_out, and_2_out, reset);
  and and_2 (and_2_out, Q2_msb, Q1);
endmodule
