// Logisim project my_encoder.circ as structural Verilog: 1 circuit, main circuit encoder
module encoder (
  input  mo_lsb,
  input  m1,
  input  m2,
  input  m3_msb,
  input  clk,
  input  En,
  input  reset,
  output enc_out
);

  wire adder0_out, adder1_out, d_ff_1_q, d_ff_2_q, d_ff_3_q, mod_6_1_q1, mod_6_1_q2_msb, mod_6_1_qo_lsb,
       multiplexer_1_out, n4_1mux_1_mux_out, t_ff_1_q;

  _4_1mux u_4_1mux_1 (
    .I0(mo_lsb), .I1(m1), .I2(m2), .I3(m3_msb), .S0(mod_6_1_qo_lsb), .S1(mod_6_1_q1), .En(En),
    .mux_out(n4_1mux_1_mux_out));
  mod_6 mod_6_1 (
    .clk(t_ff_1_q), .En(En), .reset(reset), .Q2_msb(mod_6_1_q2_msb), .Q1(mod_6_1_q1), .Qo_lsb(mod_6_1_qo_lsb));
  Multiplexer multiplexer_1 (
    .in0(n4_1mux_1_mux_out), .in1(1'b0), .out(multiplexer_1_out), .sel(mod_6_1_q2_msb), .en(En));
  D_Flip_Flop d_ff_1 (.clk(t_ff_1_q), .D(multiplexer_1_out), .Q(d_ff_1_q), .en(En), .reset(reset));  // open: Qn, preset
  D_Flip_Flop d_ff_2 (.clk(t_ff_1_q), .D(d_ff_1_q), .Q(d_ff_2_q), .en(En), .reset(reset));  // open: Qn, preset
  D_Flip_Flop d_ff_3 (.clk(t_ff_1_q), .D(d_ff_2_q), .Q(d_ff_3_q), .en(En), .reset(reset));  // open: Qn, preset
  ExactlyOne adder0 (.out(adder0_out), .in0(d_ff_1_q), .in1(d_ff_2_q), .in2(d_ff_3_q));
  xor adder1 (adder1_out, d_ff_3_q, d_ff_1_q);
  Multiplexer multiplexer_2 (.in0(adder1_out), .in1(adder0_out), .out(enc_out), .sel(t_ff_1_q), .en(En));
  T_Flip_Flop t_ff_1 (.clk(clk), .T(En), .Q(t_ff_1_q), .reset(reset), .en(En));  // open: Qn, preset

  // Notes on the sheet:
  //   required libraries: mod_6_counter , 4:1 mux
  //   p0
  //   p1
endmodule
