// Logisim project new_seq_logic.circ as structural Verilog: 1 circuit, main circuit new_seq_logic
module new_seq_logic (
  input  a,
  input  b,
  input  c,
  input  d,
  output da,
  output db,
  output dc,
  output dd
);

  wire and_1_out, and_2_out, and_3_out, and_4_out, and_5_out, and_6_out, and_7_out, and_8_out, and_9_out,
       and_10_out, and_11_out, and_12_out, and_13_out, and_14_out, and_15_out, and_16_out, and_17_out,
       and_18_out, and_19_out, and_20_out, and_21_out, and_22_out, and_23_out, and_24_out, and_25_out,
       not_1_out, not_2_out, not_3_out, not_4_out, not_5_out, not_6_out, not_7_out, not_8_out, not_9_out,
       not_10_out, not_11_out, not_12_out, not_13_out, not_14_out, not_15_out, not_16_out, not_17_out,
       not_18_out, not_19_out, not_20_out, not_21_out, or_1_out, or_2_out, or_4_out, or_5_out, or_6_out,
       or_7_out;

  not not_1 (not_1_out, a);
  and and_1 (and_1_out, not_1_out, not_2_out);
  not not_2 (not_2_out, b);
  and and_2 (and_2_out, c, d);
  and and_3 (and_3_out, b, c);
  not not_3 (not_3_out, d);
  not not_4 (not_4_out, c);
  not not_5 (not_5_out, a);
  and and_4 (and_4_out, not_5_out, not_6_out);
  not not_6 (not_6_out, b);
  not not_7 (not_7_out, d);
  and and_5 (and_5_out, a, not_8_out);
  not not_8 (not_8_out, b);
  not not_9 (not_9_out, b);
  and and_6 (and_6_out, not_9_out, not_10_out);
  not not_10 (not_10_out, c);
  not not_11 (not_11_out, b);
  and and_7 (and_7_out, not_11_out, c);
  not not_12 (not_12_out, d);
  and and_8 (and_8_out, b, not_13_out);
  not not_13 (not_13_out, c);
  not not_14 (not_14_out, d);
  not not_15 (not_15_out, c);
  not not_16 (not_16_out, a);
  and and_9 (and_9_out, not_16_out, not_17_out);
  not not_17 (not_17_out, b);
  not not_18 (not_18_out, b);
  and and_10 (and_10_out, not_18_out, c);
  not not_19 (not_19_out, c);
  and and_11 (and_11_out, a, not_20_out);
  not not_20 (not_20_out, c);
  not not_21 (not_21_out, d);
  and and_12 (and_12_out, and_1_out, and_2_out);
  and and_13 (and_13_out, and_3_out, not_3_out);
  and and_14 (and_14_out, a, not_4_out);
  and and_15 (and_15_out, a, b);
  and and_16 (and_16_out, and_4_out, not_7_out);
  and and_17 (and_17_out, and_5_out, c);
  and and_18 (and_18_out, and_6_out, d);
  and and_19 (and_19_out, and_7_out, not_12_out);
  and and_20 (and_20_out, and_8_out, not_14_out);
  and and_21 (and_21_out, a, not_15_out);
  and and_22 (and_22_out, and_9_out, c);
  and and_23 (and_23_out, and_10_out, d);
  and and_24 (and_24_out, b, not_19_out);
  and and_25 (and_25_out, and_11_out, not_21_out);
  or or_1 (or_1_out, and_12_out, and_13_out);
  or or_2 (or_2_out, and_14_out, and_15_out);
  or or_3 (db, and_16_out, and_17_out);
  or or_4 (or_4_out, and_18_out, and_19_out);
  or or_5 (or_5_out, and_20_out, and_21_out);
  or or_6 (or_6_out, and_22_out, and_23_out);
  or or_7 (or_7_out, and_24_out, and_25_out);
  or or_8 (da, or_1_out, or_2_out);
  or or_9 (dc, or_4_out, or_5_out);
  or or_10 (dd, or_6_out, or_7_out);
endmodule
