// Logisim project new_sequence_counter.circ as structural Verilog: 1 circuit, main circuit new_sequence
module new_sequence (
  input  clock,
  input  En,
  input  Reset,
  output q3_msb,
  output q2,
  output q1,
  output q0_lsb
);

  wire new_seq_logic_1_da, new_seq_logic_1_db, new_seq_logic_1_dc, new_seq_logic_1_dd;

  D_Flip_Flop d_ff_1 (.clk(clock), .D(new_seq_logic_1_da), .Q(q3_msb), .preset(Reset), .en(En));  // open: Qn, reset
  D_Flip_Flop d_ff_2 (.clk(clock), .D(new_seq_logic_1_db), .Q(q2), .preset(Reset), .en(En));  // open: Qn, reset
  new_seq_logic new_seq_logic_1 (
    .a(q3_msb), .b(q2), .c(q1), .d(q0_lsb), .da(new_seq_logic_1_da), .db(new_seq_logic_1_db),
    .dc(new_seq_logic_1_dc), .dd(new_seq_logic_1_dd));
  D_Flip_Flop d_ff_3 (.clk(clock), .D(new_seq_logic_1_dc), .Q(q1), .preset(Reset), .en(En));  // open: Qn, reset
  D_Flip_Flop d_ff_4 (.clk(clock), .D(new_seq_logic_1_dd), .Q(q0_lsb), .preset(Reset), .en(En));  // open: Qn, reset
endmodule
