// Logisim project seq_counter.circ as structural Verilog: 1 circuit, main circuit sequence_counter
module sequence_counter (
  input  clock,
  input  En,
  input  Reset,
  output q3_msb,
  output q2,
  output q1,
  output q0_lsb
);

  wire main_1_da, main_1_db, main_1_dc, main_1_dd;

  D_Flip_Flop d_ff_1 (.clk(clock), .D(main_1_da), .Q(q3_msb), .preset(Reset), .en(En));  // open: Qn, reset
  D_Flip_Flop d_ff_2 (.clk(clock), .D(main_1_db), .Q(q2), .en(En), .reset(Reset));  // open: Qn, preset
  seq_logic_main main_1 (
    .a(q3_msb), .b(q2), .c(q1), .d(q0_lsb), .da(main_1_da), .db(main_1_db), .dc(main_1_dc), .dd(main_1_dd));
  D_Flip_Flop d_ff_3 (.clk(clock), .D(main_1_dc), .Q(q1), .en(En), .reset(Reset));  // open: Qn, preset
  D_Flip_Flop d_ff_4 (.clk(clock), .D(main_1_dd), .Q(q0_lsb), .en(En), .reset(Reset));  // open: Qn, preset

  // Notes on the sheet:
  //   Sequence Generator
  //                    sequence_logic
  //   required library:seq_logic
endmodule
