// Logisim project trellis_path.circ as structural Verilog: 1 circuit, main circuit main
module main (
  input  CLK,
  input  C5,
  input  C4,
  input  C3,
  input  C2,
  input  C1,
  input  C0,
  input  C11,
  input  C10,
  input  C7,
  input  C6,
  input  C9,
  input  C8,
  input  RSET,
  output C1R1_0,
  output C1R1_1,
  output C3R1_0,
  output C3R1_1,
  output L1,
  output C4R1_0,
  output C4R1_1,
  output C5R1_0,
  output C5R1_1,
  output C2R1_0,
  output C2R1_1,
  output L0,
  output C1R2_0,
  output C1R2_1,
  output C5R2_0,
  output C5R2_1,
  output C2R2_0,
  output C2R2_1,
  output C3R2_0,
  output C3R2_1,
  output C5R3_0,
  output C5R3_1,
  output C2R3_0,
  output C2R3_1,
  output C4R2_0,
  output C4R2_1,
  output C5R4_0,
  output C5R4_1,
  output C2R4_0,
  output C2R4_1,
  output C3R3_0,
  output C3R3_1,
  output C4R3_0,
  output C4R3_1,
  output C3R4_0,
  output C3R4_1,
  output C4R4_0,
  output C4R4_1
);

  wire hamming_add_comp_1_pb0, hamming_add_comp_1_pb1, hamming_add_comp_1_s0_lsb, hamming_add_comp_1_s1,
       hamming_add_comp_1_s2, hamming_add_comp_1_s3_msb, hamming_add_comp_2_pb0, hamming_add_comp_2_pb1,
       hamming_add_comp_2_s0_lsb, hamming_add_comp_2_s1, hamming_add_comp_2_s2, hamming_add_comp_2_s3_msb,
       hamming_add_comp_3_pb0, hamming_add_comp_3_pb1, hamming_add_comp_3_s0_lsb, hamming_add_comp_3_s1,
       hamming_add_comp_3_s2, hamming_add_comp_3_s3_msb, hamming_add_comp_4_pb0, hamming_add_comp_4_pb1,
       hamming_add_comp_4_s0_lsb, hamming_add_comp_4_s1, hamming_add_comp_4_s2, hamming_add_comp_4_s3_msb,
       hamming_add_comp_5_pb0, hamming_add_comp_5_pb1, hamming_add_comp_5_s0_lsb, hamming_add_comp_5_s1,
       hamming_add_comp_5_s2, hamming_add_comp_5_s3_msb, hamming_add_comp_6_pb0, hamming_add_comp_6_pb1,
       hamming_add_comp_6_s0_lsb, hamming_add_comp_6_s1, hamming_add_comp_6_s2, hamming_add_comp_6_s3_msb,
       hamming_add_comp_7_pb0, hamming_add_comp_7_pb1, hamming_add_comp_7_s0_lsb, hamming_add_comp_7_s1,
       hamming_add_comp_7_s2, hamming_add_comp_7_s3_msb, hamming_add_comp_8_pb0, hamming_add_comp_8_pb1,
       hamming_add_comp_8_s0_lsb, hamming_add_comp_8_s1, hamming_add_comp_8_s2, hamming_add_comp_8_s3_msb,
       hamming_add_comp_9_pb0, hamming_add_comp_9_pb1, hamming_add_comp_9_s0_lsb, hamming_add_comp_9_s1,
       hamming_add_comp_9_s2, hamming_add_comp_9_s3_msb, hamming_add_comp_10_pb0, hamming_add_comp_10_pb1,
       hamming_add_comp_10_s0_lsb, hamming_add_comp_10_s1, hamming_add_comp_10_s2,
       hamming_add_comp_10_s3_msb, hamming_add_comp_11_pb0, hamming_add_comp_11_pb1,
       hamming_add_comp_11_s0_lsb, hamming_add_comp_11_s1, hamming_add_comp_11_s2,
       hamming_add_comp_11_s3_msb, hamming_add_comp_12_pb0, hamming_add_comp_12_pb1,
       hamming_add_comp_12_s0_lsb, hamming_add_comp_12_s1, hamming_add_comp_12_s2,
       hamming_add_comp_12_s3_msb, hamming_add_comp_13_pb0, hamming_add_comp_13_pb1,
       hamming_add_comp_13_s0_lsb, hamming_add_comp_13_s1, hamming_add_comp_13_s2,
       hamming_add_comp_13_s3_msb, hamming_add_comp_14_pb0, hamming_add_comp_14_pb1,
       hamming_add_comp_14_s0_lsb, hamming_add_comp_14_s1, hamming_add_comp_14_s2,
       hamming_add_comp_14_s3_msb, hamming_add_comp_15_pb0, hamming_add_comp_15_pb1,
       hamming_add_comp_15_s0_lsb, hamming_add_comp_15_s1, hamming_add_comp_15_s2,
       hamming_add_comp_15_s3_msb, hamming_add_comp_16_pb0, hamming_add_comp_16_pb1,
       hamming_add_comp_16_s0_lsb, hamming_add_comp_16_s1, hamming_add_comp_16_s2,
       hamming_add_comp_16_s3_msb, hamming_add_comp_17_pb0, hamming_add_comp_17_pb1,
       hamming_add_comp_17_s0_lsb, hamming_add_comp_17_s1, hamming_add_comp_17_s2,
       hamming_add_comp_17_s3_msb, hamming_add_comp_18_pb0, hamming_add_comp_18_pb1,
       hamming_add_comp_18_s0_lsb, hamming_add_comp_18_s1, hamming_add_comp_18_s2,
       hamming_add_comp_18_s3_msb, hamming_add_comp_19_pb0, hamming_add_comp_19_pb1,
       hamming_add_comp_19_s0_lsb, hamming_add_comp_19_s1, hamming_add_comp_19_s2,
       hamming_add_comp_19_s3_msb, hamming_add_comp_20_pb0, hamming_add_comp_20_pb1,
       hamming_add_comp_20_s0_lsb, hamming_add_comp_20_s1, hamming_add_comp_20_s2,
       hamming_add_comp_20_s3_msb, hamming_add_comp_21_pb0, hamming_add_comp_21_pb1,
       hamming_add_comp_21_s0_lsb, hamming_add_comp_21_s1, hamming_add_comp_21_s2,
       hamming_add_comp_21_s3_msb, hamming_add_comp_22_pb0, hamming_add_comp_22_pb1,
       hamming_add_comp_22_s0_lsb, hamming_add_comp_22_s1, hamming_add_comp_22_s2,
       hamming_add_comp_22_s3_msb, main_1_a_b, main_1_a_b_3, main_2_a_b, main_2_a_b_3, main_3_a_b,
       main_3_a_b_3, multiplexer_1_out, multiplexer_2_out, multiplexer_3_out, multiplexer_4_out,
       multiplexer_5_out, multiplexer_6_out, multiplexer_7_out, multiplexer_8_out, multiplexer_9_out,
       multiplexer_10_out, multiplexer_11_out, multiplexer_12_out, n8bit_reg_s0_1_b0_2, n8bit_reg_s0_1_b1_2,
       n8bit_reg_s0_1_b2_2, n8bit_reg_s0_1_b3_2, n8bit_reg_s0_1_sb0, n8bit_reg_s0_1_sb1, n8bit_reg_s0_2_b0_2,
       n8bit_reg_s0_2_b1_2, n8bit_reg_s0_2_b2_2, n8bit_reg_s0_2_b3_2, n8bit_reg_s0_3_b0_2,
       n8bit_reg_s0_3_b1_2, n8bit_reg_s0_3_b2_2, n8bit_reg_s0_3_b3_2, n8bit_reg_s0_3_sb0, n8bit_reg_s0_3_sb1,
       n8bit_reg_s0_4_b0_2, n8bit_reg_s0_4_b1_2, n8bit_reg_s0_4_b2_2, n8bit_reg_s0_4_b3_2,
       n8bit_reg_s0_4_sb0, n8bit_reg_s0_4_sb1, n8bit_reg_s0_5_b0_2, n8bit_reg_s0_5_b1_2, n8bit_reg_s0_5_b2_2,
       n8bit_reg_s0_5_b3_2, n8bit_reg_s0_5_sb0, n8bit_reg_s0_5_sb1, n8bit_reg_s0_6_b1_2, n8bit_reg_s0_6_b2_2,
       n8bit_reg_s0_6_b3_2, n8bit_reg_s0_6_sb0, n8bit_reg_s0_6_sb1, n8bit_reg_s0_7_b0_2, n8bit_reg_s0_7_b1_2,
       n8bit_reg_s0_7_b2_2, n8bit_reg_s0_7_b3_2, n8bit_reg_s0_7_pb0_2, n8bit_reg_s0_7_pb1_2,
       n8bit_reg_s1_1_b0_2, n8bit_reg_s1_1_b1_2, n8bit_reg_s1_1_b2_2, n8bit_reg_s1_1_b3_2,
       n8bit_reg_s1_1_sb0, n8bit_reg_s1_1_sb1, n8bit_reg_s1_2_b0_2, n8bit_reg_s1_2_b1_2, n8bit_reg_s1_2_b2_2,
       n8bit_reg_s1_2_b3_2, n8bit_reg_s1_2_sb0, n8bit_reg_s1_2_sb1, n8bit_reg_s1_3_b0_2, n8bit_reg_s1_3_b1_2,
       n8bit_reg_s1_3_b2_2, n8bit_reg_s1_3_b3_2, n8bit_reg_s1_3_sb0, n8bit_reg_s1_3_sb1, n8bit_reg_s1_4_b0_2,
       n8bit_reg_s1_4_b1_2, n8bit_reg_s1_4_b2_2, n8bit_reg_s1_4_b3_2, n8bit_reg_s1_4_sb0, n8bit_reg_s1_4_sb1,
       n8bit_reg_s1_5_b0_2, n8bit_reg_s1_5_b1_2, n8bit_reg_s1_5_b2_2, n8bit_reg_s1_5_b3_2,
       n8bit_reg_s1_5_sb0, n8bit_reg_s1_5_sb1, n8bit_reg_s1_6_b0_2, n8bit_reg_s1_6_b1_2, n8bit_reg_s1_6_b2_2,
       n8bit_reg_s1_6_b3_2, n8bit_reg_s1_6_pb0_2, n8bit_reg_s1_6_pb1_2, n8bit_reg_s2_1_b0_2,
       n8bit_reg_s2_1_b1_2, n8bit_reg_s2_1_b2_2, n8bit_reg_s2_1_b3_2, n8bit_reg_s2_1_sb0, n8bit_reg_s2_1_sb1,
       n8bit_reg_s2_2_b0_2, n8bit_reg_s2_2_b1_2, n8bit_reg_s2_2_b2_2, n8bit_reg_s2_2_b3_2,
       n8bit_reg_s2_2_sb0, n8bit_reg_s2_2_sb1, n8bit_reg_s2_3_b0_2, n8bit_reg_s2_3_b1_2, n8bit_reg_s2_3_b2_2,
       n8bit_reg_s2_3_b3_2, n8bit_reg_s2_3_sb0, n8bit_reg_s2_3_sb1, n8bit_reg_s2_4_b0_2, n8bit_reg_s2_4_b1_2,
       n8bit_reg_s2_4_b2_2, n8bit_reg_s2_4_b3_2, n8bit_reg_s2_4_sb0, n8bit_reg_s2_4_sb1, n8bit_reg_s2_5_b0_2,
       n8bit_reg_s2_5_b1_2, n8bit_reg_s2_5_b2_2, n8bit_reg_s2_5_b3_2, n8bit_reg_s2_5_pb0_2,
       n8bit_reg_s2_5_pb1_2, n8bit_reg_s3_1_b0_2, n8bit_reg_s3_1_b1_2, n8bit_reg_s3_1_b2_2,
       n8bit_reg_s3_1_b3_2, n8bit_reg_s3_1_sb0, n8bit_reg_s3_1_sb1, n8bit_reg_s3_2_b0_2, n8bit_reg_s3_2_b1_2,
       n8bit_reg_s3_2_b2_2, n8bit_reg_s3_2_b3_2, n8bit_reg_s3_2_sb0, n8bit_reg_s3_2_sb1, n8bit_reg_s3_3_b0_2,
       n8bit_reg_s3_3_b1_2, n8bit_reg_s3_3_b2_2, n8bit_reg_s3_3_b3_2, n8bit_reg_s3_3_sb0, n8bit_reg_s3_3_sb1,
       n8bit_reg_s3_4_b0_2, n8bit_reg_s3_4_b1_2, n8bit_reg_s3_4_b2_2, n8bit_reg_s3_4_b3_2,
       n8bit_reg_s3_4_sb0, n8bit_reg_s3_4_sb1, n8bit_reg_s3_5_b0_2, n8bit_reg_s3_5_b1_2, n8bit_reg_s3_5_b2_2,
       n8bit_reg_s3_5_b3_2, n8bit_reg_s3_5_pb0_2, n8bit_reg_s3_5_pb1_2, or_1_out, or_2_out, or_3_out;

  _8bit_reg_S0 u_8bit_reg_s0_1 (
    .clk(CLK), .RST(RSET), .b0_2(n8bit_reg_s0_1_b0_2), .b1_2(n8bit_reg_s0_1_b1_2),
    .b2_2(n8bit_reg_s0_1_b2_2), .b3_2(n8bit_reg_s0_1_b3_2), .sb0(n8bit_reg_s0_1_sb0), .sb1(n8bit_reg_s0_1_sb1));  // open: b0, b1, b2, b3, pb0, pb1, pb0_2, pb1_2
  hamming_add_comp hamming_add_comp_1 (
    .EXT(1'b0), .B01(n8bit_reg_s0_1_b1_2), .B02(n8bit_reg_s0_1_b2_2), .B03(n8bit_reg_s0_1_b3_2), .CIN0(C10),
    .IN00(1'b0), .CIN1(C11), .IN01(1'b0), .B10(n8bit_reg_s0_1_b0_2), .B11(n8bit_reg_s0_1_b1_2),
    .B12(n8bit_reg_s0_1_b2_2), .B13(n8bit_reg_s0_1_b3_2), .IN10(1'b0), .IN11(1'b0), .AS0(n8bit_reg_s0_1_sb0),
    .AS1(n8bit_reg_s0_1_sb1), .BS0(n8bit_reg_s0_1_sb0), .BS1(n8bit_reg_s0_1_sb1), .B00(n8bit_reg_s0_1_b0_2),
    .S0_lsb(hamming_add_comp_1_s0_lsb), .S1(hamming_add_comp_1_s1), .S2(hamming_add_comp_1_s2),
    .S3_msb(hamming_add_comp_1_s3_msb), .PB0(hamming_add_comp_1_pb0), .PB1(hamming_add_comp_1_pb1));
  hamming_add_comp hamming_add_comp_2 (
    .EXT(1'b0), .B01(n8bit_reg_s0_1_b1_2), .B02(n8bit_reg_s0_1_b2_2), .B03(n8bit_reg_s0_1_b3_2), .CIN0(C10),
    .IN00(1'b1), .CIN1(C11), .IN01(1'b1), .B10(n8bit_reg_s0_1_b0_2), .B11(n8bit_reg_s0_1_b1_2),
    .B12(n8bit_reg_s0_1_b2_2), .B13(n8bit_reg_s0_1_b3_2), .IN10(1'b1), .IN11(1'b1), .AS0(n8bit_reg_s0_1_sb1),
    .AS1(n8bit_reg_s0_1_sb1), .BS0(n8bit_reg_s0_1_sb1), .BS1(n8bit_reg_s0_1_sb1), .B00(n8bit_reg_s0_1_b0_2),
    .S0_lsb(hamming_add_comp_2_s0_lsb), .S1(hamming_add_comp_2_s1), .S2(hamming_add_comp_2_s2),
    .S3_msb(hamming_add_comp_2_s3_msb), .PB0(hamming_add_comp_2_pb0), .PB1(hamming_add_comp_2_pb1));
  _8bit_reg_S0 u_8bit_reg_s0_2 (
    .clk(CLK), .b0(hamming_add_comp_1_s0_lsb), .b1(hamming_add_comp_1_s1), .b2(hamming_add_comp_1_s2),
    .b3(hamming_add_comp_1_s3_msb), .pb0(hamming_add_comp_1_pb0), .pb1(hamming_add_comp_1_pb1), .RST(RSET),
    .b0_2(n8bit_reg_s0_2_b0_2), .b1_2(n8bit_reg_s0_2_b1_2), .b2_2(n8bit_reg_s0_2_b2_2),
    .b3_2(n8bit_reg_s0_2_b3_2), .pb0_2(C1R1_0), .pb1_2(C1R1_1));  // open: sb0, sb1
  _8bit_reg_S1 u_8bit_reg_s1_1 (
    .clk(CLK), .b0(hamming_add_comp_2_s0_lsb), .b1(hamming_add_comp_2_s1), .b2(hamming_add_comp_2_s2),
    .b3(hamming_add_comp_2_s3_msb), .pb0(hamming_add_comp_2_pb0), .pb1(hamming_add_comp_2_pb1), .RST(RSET),
    .b0_2(n8bit_reg_s1_1_b0_2), .b1_2(n8bit_reg_s1_1_b1_2), .b2_2(n8bit_reg_s1_1_b2_2),
    .b3_2(n8bit_reg_s1_1_b3_2), .pb0_2(C1R2_0), .pb1_2(C1R2_1), .sb0(n8bit_reg_s1_1_sb0),
    .sb1(n8bit_reg_s1_1_sb1));
  hamming_add_comp hamming_add_comp_3 (
    .EXT(1'b0), .B01(n8bit_reg_s0_2_b1_2), .B02(n8bit_reg_s0_2_b2_2), .B03(n8bit_reg_s0_2_b3_2), .CIN0(C8),
    .IN00(1'b0), .CIN1(C9), .IN01(1'b0), .B10(n8bit_reg_s0_2_b0_2), .B11(n8bit_reg_s0_2_b1_2),
    .B12(n8bit_reg_s0_2_b2_2), .B13(n8bit_reg_s0_2_b3_2), .IN10(1'b0), .IN11(1'b0), .AS0(C1R1_0),
    .AS1(C1R1_1), .BS0(C1R1_0), .BS1(C1R1_1), .B00(n8bit_reg_s0_2_b0_2), .S0_lsb(hamming_add_comp_3_s0_lsb),
    .S1(hamming_add_comp_3_s1), .S2(hamming_add_comp_3_s2), .S3_msb(hamming_add_comp_3_s3_msb),
    .PB0(hamming_add_comp_3_pb0), .PB1(hamming_add_comp_3_pb1));
  hamming_add_comp hamming_add_comp_4 (
    .EXT(1'b0), .B01(n8bit_reg_s0_2_b1_2), .B02(n8bit_reg_s0_2_b2_2), .B03(n8bit_reg_s0_2_b3_2), .CIN0(C8),
    .IN00(1'b1), .CIN1(C9), .IN01(1'b1), .B10(n8bit_reg_s0_2_b0_2), .B11(n8bit_reg_s0_2_b1_2),
    .B12(n8bit_reg_s0_2_b2_2), .B13(n8bit_reg_s0_2_b3_2), .IN10(1'b1), .IN11(1'b1), .AS0(C1R1_1),
    .AS1(C1R1_1), .BS0(C1R1_1), .BS1(C1R1_1), .B00(n8bit_reg_s0_2_b0_2), .S0_lsb(hamming_add_comp_4_s0_lsb),
    .S1(hamming_add_comp_4_s1), .S2(hamming_add_comp_4_s2), .S3_msb(hamming_add_comp_4_s3_msb),
    .PB0(hamming_add_comp_4_pb0), .PB1(hamming_add_comp_4_pb1));
  hamming_add_comp hamming_add_comp_5 (
    .EXT(1'b0), .B01(n8bit_reg_s1_1_b1_2), .B02(n8bit_reg_s1_1_b2_2), .B03(n8bit_reg_s1_1_b3_2), .CIN0(C8),
    .IN00(1'b1), .CIN1(C9), .IN01(1'b0), .B10(n8bit_reg_s1_1_b0_2), .B11(n8bit_reg_s1_1_b1_2),
    .B12(n8bit_reg_s1_1_b2_2), .B13(n8bit_reg_s1_1_b3_2), .IN10(1'b1), .IN11(1'b0), .AS0(n8bit_reg_s1_1_sb0),
    .AS1(n8bit_reg_s1_1_sb1), .BS0(n8bit_reg_s1_1_sb0), .BS1(n8bit_reg_s1_1_sb1), .B00(n8bit_reg_s1_1_b0_2),
    .S0_lsb(hamming_add_comp_5_s0_lsb), .S1(hamming_add_comp_5_s1), .S2(hamming_add_comp_5_s2),
    .S3_msb(hamming_add_comp_5_s3_msb), .PB0(hamming_add_comp_5_pb0), .PB1(hamming_add_comp_5_pb1));
  hamming_add_comp hamming_add_comp_6 (
    .EXT(1'b0), .B01(n8bit_reg_s1_1_b1_2), .B02(n8bit_reg_s1_1_b2_2), .B03(n8bit_reg_s1_1_b3_2), .CIN0(C8),
    .IN00(1'b0), .CIN1(C9), .IN01(1'b1), .B10(n8bit_reg_s1_1_b0_2), .B11(n8bit_reg_s1_1_b1_2),
    .B12(n8bit_reg_s1_1_b2_2), .B13(n8bit_reg_s1_1_b3_2), .IN10(1'b0), .IN11(1'b1), .AS0(n8bit_reg_s1_1_sb0),
    .AS1(n8bit_reg_s1_1_sb1), .BS0(n8bit_reg_s1_1_sb0), .BS1(n8bit_reg_s1_1_sb1), .B00(n8bit_reg_s1_1_b0_2),
    .S0_lsb(hamming_add_comp_6_s0_lsb), .S1(hamming_add_comp_6_s1), .S2(hamming_add_comp_6_s2),
    .S3_msb(hamming_add_comp_6_s3_msb), .PB0(hamming_add_comp_6_pb0), .PB1(hamming_add_comp_6_pb1));
  _8bit_reg_S0 u_8bit_reg_s0_3 (
    .clk(CLK), .b0(hamming_add_comp_3_s0_lsb), .b1(hamming_add_comp_3_s1), .b2(hamming_add_comp_3_s2),
    .b3(hamming_add_comp_3_s3_msb), .pb0(hamming_add_comp_3_pb0), .pb1(hamming_add_comp_3_pb1), .RST(RSET),
    .b0_2(n8bit_reg_s0_3_b0_2), .b1_2(n8bit_reg_s0_3_b1_2), .b2_2(n8bit_reg_s0_3_b2_2),
    .b3_2(n8bit_reg_s0_3_b3_2), .pb0_2(C2R1_0), .pb1_2(C2R1_1), .sb0(n8bit_reg_s0_3_sb0),
    .sb1(n8bit_reg_s0_3_sb1));
  _8bit_reg_S1 u_8bit_reg_s1_2 (
    .clk(CLK), .b0(hamming_add_comp_4_s0_lsb), .b1(hamming_add_comp_4_s1), .b2(hamming_add_comp_4_s2),
    .b3(hamming_add_comp_4_s3_msb), .pb0(hamming_add_comp_4_pb0), .pb1(hamming_add_comp_4_pb1), .RST(RSET),
    .b0_2(n8bit_reg_s1_2_b0_2), .b1_2(n8bit_reg_s1_2_b1_2), .b2_2(n8bit_reg_s1_2_b2_2),
    .b3_2(n8bit_reg_s1_2_b3_2), .pb0_2(C2R2_0), .pb1_2(C2R2_1), .sb0(n8bit_reg_s1_2_sb0),
    .sb1(n8bit_reg_s1_2_sb1));
  _8bit_reg_S2 u_8bit_reg_s2_1 (
    .clk(CLK), .b0(hamming_add_comp_5_s0_lsb), .b1(hamming_add_comp_5_s1), .b2(hamming_add_comp_5_s2),
    .b3(hamming_add_comp_5_s3_msb), .pb0(hamming_add_comp_5_pb0), .pb1(hamming_add_comp_5_pb1), .RST(RSET),
    .b0_2(n8bit_reg_s2_1_b0_2), .b1_2(n8bit_reg_s2_1_b1_2), .b2_2(n8bit_reg_s2_1_b2_2),
    .b3_2(n8bit_reg_s2_1_b3_2), .pb0_2(C2R3_0), .pb1_2(C2R3_1), .sb0(n8bit_reg_s2_1_sb0),
    .sb1(n8bit_reg_s2_1_sb1));
  _8bit_reg_S3 u_8bit_reg_s3_1 (
    .clk(CLK), .b0(hamming_add_comp_6_s0_lsb), .b1(hamming_add_comp_6_s1), .b2(hamming_add_comp_6_s2),
    .b3(hamming_add_comp_6_s3_msb), .pb0(hamming_add_comp_6_pb0), .pb1(hamming_add_comp_6_pb1), .RST(RSET),
    .b0_2(n8bit_reg_s3_1_b0_2), .b1_2(n8bit_reg_s3_1_b1_2), .b2_2(n8bit_reg_s3_1_b2_2),
    .b3_2(n8bit_reg_s3_1_b3_2), .pb0_2(C2R4_0), .pb1_2(C2R4_1), .sb0(n8bit_reg_s3_1_sb0),
    .sb1(n8bit_reg_s3_1_sb1));
  hamming_add_comp hamming_add_comp_7 (
    .EXT(1'b0), .B01(n8bit_reg_s0_3_b1_2), .B02(n8bit_reg_s0_3_b2_2), .B03(n8bit_reg_s0_3_b3_2), .CIN0(C6),
    .IN00(1'b0), .CIN1(C7), .IN01(1'b0), .B10(n8bit_reg_s2_1_b0_2), .B11(n8bit_reg_s2_1_b1_2),
    .B12(n8bit_reg_s2_1_b2_2), .B13(n8bit_reg_s2_1_b3_2), .IN10(1'b1), .IN11(1'b1), .AS0(n8bit_reg_s0_3_sb0),
    .AS1(n8bit_reg_s0_3_sb1), .BS0(n8bit_reg_s2_1_sb0), .BS1(n8bit_reg_s2_1_sb1), .B00(n8bit_reg_s0_3_b0_2),
    .S0_lsb(hamming_add_comp_7_s0_lsb), .S1(hamming_add_comp_7_s1), .S2(hamming_add_comp_7_s2),
    .S3_msb(hamming_add_comp_7_s3_msb), .PB0(hamming_add_comp_7_pb0), .PB1(hamming_add_comp_7_pb1));
  hamming_add_comp hamming_add_comp_8 (
    .EXT(1'b0), .B01(n8bit_reg_s0_3_b1_2), .B02(n8bit_reg_s0_3_b2_2), .B03(n8bit_reg_s0_3_b3_2), .CIN0(C6),
    .IN00(1'b1), .CIN1(C7), .IN01(1'b1), .B10(n8bit_reg_s2_1_b0_2), .B11(n8bit_reg_s2_1_b1_2),
    .B12(n8bit_reg_s2_1_b2_2), .B13(n8bit_reg_s2_1_b3_2), .IN10(1'b0), .IN11(1'b0), .AS0(n8bit_reg_s0_3_sb0),
    .AS1(n8bit_reg_s0_3_sb1), .BS0(n8bit_reg_s2_1_sb0), .BS1(n8bit_reg_s2_1_sb1), .B00(n8bit_reg_s0_3_b0_2),
    .S0_lsb(hamming_add_comp_8_s0_lsb), .S1(hamming_add_comp_8_s1), .S2(hamming_add_comp_8_s2),
    .S3_msb(hamming_add_comp_8_s3_msb), .PB0(hamming_add_comp_8_pb0), .PB1(hamming_add_comp_8_pb1));
  hamming_add_comp hamming_add_comp_9 (
    .EXT(1'b0), .B01(n8bit_reg_s1_2_b1_2), .B02(n8bit_reg_s1_2_b2_2), .B03(n8bit_reg_s1_2_b3_2), .CIN0(C6),
    .IN00(1'b1), .CIN1(C7), .IN01(1'b0), .B10(n8bit_reg_s3_1_b0_2), .B11(n8bit_reg_s3_1_b1_2),
    .B12(n8bit_reg_s3_1_b2_2), .B13(n8bit_reg_s3_1_b3_2), .IN10(1'b0), .IN11(1'b1), .AS0(n8bit_reg_s1_2_sb0),
    .AS1(n8bit_reg_s1_2_sb1), .BS0(n8bit_reg_s3_1_sb0), .BS1(n8bit_reg_s3_1_sb1), .B00(n8bit_reg_s1_2_b0_2),
    .S0_lsb(hamming_add_comp_9_s0_lsb), .S1(hamming_add_comp_9_s1), .S2(hamming_add_comp_9_s2),
    .S3_msb(hamming_add_comp_9_s3_msb), .PB0(hamming_add_comp_9_pb0), .PB1(hamming_add_comp_9_pb1));
  hamming_add_comp hamming_add_comp_10 (
    .EXT(1'b0), .B01(n8bit_reg_s1_2_b1_2), .B02(n8bit_reg_s1_2_b2_2), .B03(n8bit_reg_s1_2_b3_2), .CIN0(C6),
    .IN00(1'b0), .CIN1(C7), .IN01(1'b1), .B10(n8bit_reg_s3_1_b0_2), .B11(n8bit_reg_s3_1_b1_2),
    .B12(n8bit_reg_s3_1_b2_2), .B13(n8bit_reg_s3_1_b3_2), .IN10(1'b1), .IN11(1'b0), .AS0(n8bit_reg_s1_2_sb0),
    .AS1(n8bit_reg_s1_2_sb1), .BS0(n8bit_reg_s3_1_sb0), .BS1(n8bit_reg_s3_1_sb1), .B00(n8bit_reg_s1_2_b0_2),
    .S0_lsb(hamming_add_comp_10_s0_lsb), .S1(hamming_add_comp_10_s1), .S2(hamming_add_comp_10_s2),
    .S3_msb(hamming_add_comp_10_s3_msb), .PB0(hamming_add_comp_10_pb0), .PB1(hamming_add_comp_10_pb1));
  _8bit_reg_S0 u_8bit_reg_s0_4 (
    .clk(CLK), .b0(hamming_add_comp_7_s0_lsb), .b1(hamming_add_comp_7_s1), .b2(hamming_add_comp_7_s2),
    .b3(hamming_add_comp_7_s3_msb), .pb0(hamming_add_comp_7_pb0), .pb1(hamming_add_comp_7_pb1), .RST(RSET),
    .b0_2(n8bit_reg_s0_4_b0_2), .b1_2(n8bit_reg_s0_4_b1_2), .b2_2(n8bit_reg_s0_4_b2_2),
    .b3_2(n8bit_reg_s0_4_b3_2), .pb0_2(C3R1_0), .pb1_2(C3R1_1), .sb0(n8bit_reg_s0_4_sb0),
    .sb1(n8bit_reg_s0_4_sb1));
  _8bit_reg_S1 u_8bit_reg_s1_3 (
    .clk(CLK), .b0(hamming_add_comp_8_s0_lsb), .b1(hamming_add_comp_8_s1), .b2(hamming_add_comp_8_s2),
    .b3(hamming_add_comp_8_s3_msb), .pb0(hamming_add_comp_8_pb0), .pb1(hamming_add_comp_8_pb1), .RST(RSET),
    .b0_2(n8bit_reg_s1_3_b0_2), .b1_2(n8bit_reg_s1_3_b1_2), .b2_2(n8bit_reg_s1_3_b2_2),
    .b3_2(n8bit_reg_s1_3_b3_2), .pb0_2(C3R2_0), .pb1_2(C3R2_1), .sb0(n8bit_reg_s1_3_sb0),
    .sb1(n8bit_reg_s1_3_sb1));
  _8bit_reg_S2 u_8bit_reg_s2_2 (
    .clk(CLK), .b0(hamming_add_comp_9_s0_lsb), .b1(hamming_add_comp_9_s1), .b2(hamming_add_comp_9_s2),
    .b3(hamming_add_comp_9_s3_msb), .pb0(hamming_add_comp_9_pb0), .pb1(hamming_add_comp_9_pb1), .RST(RSET),
    .b0_2(n8bit_reg_s2_2_b0_2), .b1_2(n8bit_reg_s2_2_b1_2), .b2_2(n8bit_reg_s2_2_b2_2),
    .b3_2(n8bit_reg_s2_2_b3_2), .pb0_2(C3R3_0), .pb1_2(C3R3_1), .sb0(n8bit_reg_s2_2_sb0),
    .sb1(n8bit_reg_s2_2_sb1));
  _8bit_reg_S3 u_8bit_reg_s3_2 (
    .clk(CLK), .b0(hamming_add_comp_10_s0_lsb), .b1(hamming_add_comp_10_s1), .b2(hamming_add_comp_10_s2),
    .b3(hamming_add_comp_10_s3_msb), .pb0(hamming_add_comp_10_pb0), .pb1(hamming_add_comp_10_pb1),
    .RST(RSET), .b0_2(n8bit_reg_s3_2_b0_2), .b1_2(n8bit_reg_s3_2_b1_2), .b2_2(n8bit_reg_s3_2_b2_2),
    .b3_2(n8bit_reg_s3_2_b3_2), .pb0_2(C3R4_0), .pb1_2(C3R4_1), .sb0(n8bit_reg_s3_2_sb0),
    .sb1(n8bit_reg_s3_2_sb1));
  hamming_add_comp hamming_add_comp_11 (
    .EXT(1'b0), .B01(n8bit_reg_s0_4_b1_2), .B02(n8bit_reg_s0_4_b2_2), .B03(n8bit_reg_s0_4_b3_2), .CIN0(C4),
    .IN00(1'b0), .CIN1(C5), .IN01(1'b0), .B10(n8bit_reg_s2_2_b0_2), .B11(n8bit_reg_s2_2_b1_2),
    .B12(n8bit_reg_s2_2_b2_2), .B13(n8bit_reg_s2_2_b3_2), .IN10(1'b1), .IN11(1'b1), .AS0(n8bit_reg_s0_4_sb0),
    .AS1(n8bit_reg_s0_4_sb1), .BS0(n8bit_reg_s2_2_sb0), .BS1(n8bit_reg_s2_2_sb1), .B00(n8bit_reg_s0_4_b0_2),
    .S0_lsb(hamming_add_comp_11_s0_lsb), .S1(hamming_add_comp_11_s1), .S2(hamming_add_comp_11_s2),
    .S3_msb(hamming_add_comp_11_s3_msb), .PB0(hamming_add_comp_11_pb0), .PB1(hamming_add_comp_11_pb1));
  hamming_add_comp hamming_add_comp_12 (
    .EXT(1'b0), .B01(n8bit_reg_s0_4_b1_2), .B02(n8bit_reg_s0_4_b2_2), .B03(n8bit_reg_s0_4_b3_2), .CIN0(C4),
    .IN00(1'b1), .CIN1(C5), .IN01(1'b1), .B10(n8bit_reg_s2_2_b0_2), .B11(n8bit_reg_s2_2_b1_2),
    .B12(n8bit_reg_s2_2_b2_2), .B13(n8bit_reg_s2_2_b3_2), .IN10(1'b0), .IN11(1'b0), .AS0(n8bit_reg_s0_4_sb0),
    .AS1(n8bit_reg_s0_4_sb1), .BS0(n8bit_reg_s2_2_sb0), .BS1(n8bit_reg_s2_2_sb1), .B00(n8bit_reg_s0_4_b0_2),
    .S0_lsb(hamming_add_comp_12_s0_lsb), .S1(hamming_add_comp_12_s1), .S2(hamming_add_comp_12_s2),
    .S3_msb(hamming_add_comp_12_s3_msb), .PB0(hamming_add_comp_12_pb0), .PB1(hamming_add_comp_12_pb1));
  hamming_add_comp hamming_add_comp_13 (
    .EXT(1'b0), .B01(n8bit_reg_s1_3_b1_2), .B02(n8bit_reg_s1_3_b2_2), .B03(n8bit_reg_s1_3_b3_2), .CIN0(C4),
    .IN00(1'b1), .CIN1(C5), .IN01(1'b0), .B10(n8bit_reg_s3_2_b0_2), .B11(n8bit_reg_s3_2_b1_2),
    .B12(n8bit_reg_s3_2_b2_2), .B13(n8bit_reg_s3_2_b3_2), .IN10(1'b0), .IN11(1'b1), .AS0(n8bit_reg_s1_3_sb0),
    .AS1(n8bit_reg_s1_3_sb1), .BS0(n8bit_reg_s3_2_sb0), .BS1(n8bit_reg_s3_2_sb1), .B00(n8bit_reg_s1_3_b0_2),
    .S0_lsb(hamming_add_comp_13_s0_lsb), .S1(hamming_add_comp_13_s1), .S2(hamming_add_comp_13_s2),
    .S3_msb(hamming_add_comp_13_s3_msb), .PB0(hamming_add_comp_13_pb0), .PB1(hamming_add_comp_13_pb1));
  hamming_add_comp hamming_add_comp_14 (
    .EXT(1'b0), .B01(n8bit_reg_s1_3_b1_2), .B02(n8bit_reg_s1_3_b2_2), .B03(n8bit_reg_s1_3_b3_2), .CIN0(C4),
    .IN00(1'b0), .CIN1(C5), .IN01(1'b1), .B10(n8bit_reg_s3_2_b0_2), .B11(n8bit_reg_s3_2_b1_2),
    .B12(n8bit_reg_s3_2_b2_2), .B13(n8bit_reg_s3_2_b3_2), .IN10(1'b1), .IN11(1'b0), .AS0(n8bit_reg_s1_3_sb0),
    .AS1(n8bit_reg_s1_3_sb1), .BS0(n8bit_reg_s3_2_sb0), .BS1(n8bit_reg_s3_2_sb1), .B00(n8bit_reg_s1_3_b0_2),
    .S0_lsb(hamming_add_comp_14_s0_lsb), .S1(hamming_add_comp_14_s1), .S2(hamming_add_comp_14_s2),
    .S3_msb(hamming_add_comp_14_s3_msb), .PB0(hamming_add_comp_14_pb0), .PB1(hamming_add_comp_14_pb1));
  _8bit_reg_S0 u_8bit_reg_s0_5 (
    .clk(CLK), .b0(hamming_add_comp_11_s0_lsb), .b1(hamming_add_comp_11_s1), .b2(hamming_add_comp_11_s2),
    .b3(hamming_add_comp_11_s3_msb), .pb0(hamming_add_comp_11_pb0), .pb1(hamming_add_comp_11_pb1),
    .RST(RSET), .b0_2(n8bit_reg_s0_5_b0_2), .b1_2(n8bit_reg_s0_5_b1_2), .b2_2(n8bit_reg_s0_5_b2_2),
    .b3_2(n8bit_reg_s0_5_b3_2), .pb0_2(C4R1_0), .pb1_2(C4R1_1), .sb0(n8bit_reg_s0_5_sb0),
    .sb1(n8bit_reg_s0_5_sb1));
  _8bit_reg_S1 u_8bit_reg_s1_4 (
    .clk(CLK), .b0(hamming_add_comp_12_s0_lsb), .b1(hamming_add_comp_12_s1), .b2(hamming_add_comp_12_s2),
    .b3(hamming_add_comp_12_s3_msb), .pb0(hamming_add_comp_12_pb0), .pb1(hamming_add_comp_12_pb1),
    .RST(RSET), .b0_2(n8bit_reg_s1_4_b0_2), .b1_2(n8bit_reg_s1_4_b1_2), .b2_2(n8bit_reg_s1_4_b2_2),
    .b3_2(n8bit_reg_s1_4_b3_2), .pb0_2(C4R2_0), .pb1_2(C4R2_1), .sb0(n8bit_reg_s1_4_sb0),
    .sb1(n8bit_reg_s1_4_sb1));
  _8bit_reg_S2 u_8bit_reg_s2_3 (
    .clk(CLK), .b0(hamming_add_comp_13_s0_lsb), .b1(hamming_add_comp_13_s1), .b2(hamming_add_comp_13_s2),
    .b3(hamming_add_comp_13_s3_msb), .pb0(hamming_add_comp_13_pb0), .pb1(hamming_add_comp_13_pb1),
    .RST(RSET), .b0_2(n8bit_reg_s2_3_b0_2), .b1_2(n8bit_reg_s2_3_b1_2), .b2_2(n8bit_reg_s2_3_b2_2),
    .b3_2(n8bit_reg_s2_3_b3_2), .pb0_2(C4R3_0), .pb1_2(C4R3_1), .sb0(n8bit_reg_s2_3_sb0),
    .sb1(n8bit_reg_s2_3_sb1));
  _8bit_reg_S3 u_8bit_reg_s3_3 (
    .clk(CLK), .b0(hamming_add_comp_14_s0_lsb), .b1(hamming_add_comp_14_s1), .b2(hamming_add_comp_14_s2),
    .b3(hamming_add_comp_14_s3_msb), .pb0(hamming_add_comp_14_pb0), .pb1(hamming_add_comp_14_pb1),
    .RST(RSET), .b0_2(n8bit_reg_s3_3_b0_2), .b1_2(n8bit_reg_s3_3_b1_2), .b2_2(n8bit_reg_s3_3_b2_2),
    .b3_2(n8bit_reg_s3_3_b3_2), .pb0_2(C4R4_0), .pb1_2(C4R4_1), .sb0(n8bit_reg_s3_3_sb0),
    .sb1(n8bit_reg_s3_3_sb1));
  hamming_add_comp hamming_add_comp_15 (
    .EXT(1'b0), .B01(n8bit_reg_s0_5_b1_2), .B02(n8bit_reg_s0_5_b2_2), .B03(n8bit_reg_s0_5_b3_2), .CIN0(C2),
    .IN00(1'b0), .CIN1(C3), .IN01(1'b0), .B10(n8bit_reg_s2_3_b0_2), .B11(n8bit_reg_s2_3_b1_2),
    .B12(n8bit_reg_s2_3_b2_2), .B13(n8bit_reg_s2_3_b3_2), .IN10(1'b1), .IN11(1'b1), .AS0(n8bit_reg_s0_5_sb0),
    .AS1(n8bit_reg_s0_5_sb1), .BS0(n8bit_reg_s2_3_sb0), .BS1(n8bit_reg_s2_3_sb1), .B00(n8bit_reg_s0_5_b0_2),
    .S0_lsb(hamming_add_comp_15_s0_lsb), .S1(hamming_add_comp_15_s1), .S2(hamming_add_comp_15_s2),
    .S3_msb(hamming_add_comp_15_s3_msb), .PB0(hamming_add_comp_15_pb0), .PB1(hamming_add_comp_15_pb1));
  hamming_add_comp hamming_add_comp_16 (
    .EXT(1'b0), .B01(n8bit_reg_s0_5_b1_2), .B02(n8bit_reg_s0_5_b2_2), .B03(n8bit_reg_s0_5_b3_2), .CIN0(C2),
    .IN00(1'b1), .CIN1(C3), .IN01(1'b1), .B10(n8bit_reg_s2_3_b0_2), .B11(n8bit_reg_s2_3_b1_2),
    .B12(n8bit_reg_s2_3_b2_2), .B13(n8bit_reg_s2_3_b3_2), .IN10(1'b0), .IN11(1'b0), .AS0(n8bit_reg_s0_5_sb0),
    .AS1(n8bit_reg_s0_5_sb1), .BS0(n8bit_reg_s2_3_sb0), .BS1(n8bit_reg_s2_3_sb1), .B00(n8bit_reg_s0_5_b0_2),
    .S0_lsb(hamming_add_comp_16_s0_lsb), .S1(hamming_add_comp_16_s1), .S2(hamming_add_comp_16_s2),
    .S3_msb(hamming_add_comp_16_s3_msb), .PB0(hamming_add_comp_16_pb0), .PB1(hamming_add_comp_16_pb1));
  hamming_add_comp hamming_add_comp_17 (
    .EXT(1'b0), .B01(n8bit_reg_s1_4_b1_2), .B02(n8bit_reg_s1_4_b2_2), .B03(n8bit_reg_s1_4_b3_2), .CIN0(C2),
    .IN00(1'b1), .CIN1(C3), .IN01(1'b0), .B10(n8bit_reg_s3_3_b0_2), .B11(n8bit_reg_s3_3_b1_2),
    .B12(n8bit_reg_s3_3_b2_2), .B13(n8bit_reg_s3_3_b3_2), .IN10(1'b0), .IN11(1'b1), .AS0(n8bit_reg_s1_4_sb0),
    .AS1(n8bit_reg_s1_4_sb1), .BS0(n8bit_reg_s3_3_sb0), .BS1(n8bit_reg_s3_3_sb1), .B00(n8bit_reg_s1_4_b0_2),
    .S0_lsb(hamming_add_comp_17_s0_lsb), .S1(hamming_add_comp_17_s1), .S2(hamming_add_comp_17_s2),
    .S3_msb(hamming_add_comp_17_s3_msb), .PB0(hamming_add_comp_17_pb0), .PB1(hamming_add_comp_17_pb1));
  hamming_add_comp hamming_add_comp_18 (
    .EXT(1'b0), .B01(n8bit_reg_s1_4_b1_2), .B02(n8bit_reg_s1_4_b2_2), .B03(n8bit_reg_s1_4_b3_2), .CIN0(C2),
    .IN00(1'b0), .CIN1(C3), .IN01(1'b1), .B10(n8bit_reg_s3_3_b0_2), .B11(n8bit_reg_s3_3_b1_2),
    .B12(n8bit_reg_s3_3_b2_2), .B13(n8bit_reg_s3_3_b3_2), .IN10(1'b1), .IN11(1'b0), .AS0(n8bit_reg_s1_4_sb0),
    .AS1(n8bit_reg_s1_4_sb1), .BS0(n8bit_reg_s3_3_sb0), .BS1(n8bit_reg_s3_3_sb1), .B00(n8bit_reg_s1_4_b0_2),
    .S0_lsb(hamming_add_comp_18_s0_lsb), .S1(hamming_add_comp_18_s1), .S2(hamming_add_comp_18_s2),
    .S3_msb(hamming_add_comp_18_s3_msb), .PB0(hamming_add_comp_18_pb0), .PB1(hamming_add_comp_18_pb1));
  _8bit_reg_S0 u_8bit_reg_s0_6 (
    .clk(CLK), .b0(hamming_add_comp_15_s0_lsb), .b1(hamming_add_comp_15_s1), .b2(hamming_add_comp_15_s2),
    .b3(hamming_add_comp_15_s3_msb), .pb0(hamming_add_comp_15_pb0), .pb1(hamming_add_comp_15_pb1),
    .RST(RSET), .b1_2(n8bit_reg_s0_6_b1_2), .b2_2(n8bit_reg_s0_6_b2_2), .b3_2(n8bit_reg_s0_6_b3_2),
    .pb0_2(C5R1_0), .pb1_2(C5R1_1), .sb0(n8bit_reg_s0_6_sb0), .sb1(n8bit_reg_s0_6_sb1));  // open: b0_2
  _8bit_reg_S1 u_8bit_reg_s1_5 (
    .clk(CLK), .b0(hamming_add_comp_16_s0_lsb), .b1(hamming_add_comp_16_s1), .b2(hamming_add_comp_16_s2),
    .b3(hamming_add_comp_16_s3_msb), .pb0(hamming_add_comp_16_pb0), .pb1(hamming_add_comp_16_pb1),
    .RST(RSET), .b0_2(n8bit_reg_s1_5_b0_2), .b1_2(n8bit_reg_s1_5_b1_2), .b2_2(n8bit_reg_s1_5_b2_2),
    .b3_2(n8bit_reg_s1_5_b3_2), .pb0_2(C5R2_0), .pb1_2(C5R2_1), .sb0(n8bit_reg_s1_5_sb0),
    .sb1(n8bit_reg_s1_5_sb1));
  _8bit_reg_S2 u_8bit_reg_s2_4 (
    .clk(CLK), .b0(hamming_add_comp_17_s0_lsb), .b1(hamming_add_comp_17_s1), .b2(hamming_add_comp_17_s2),
    .b3(hamming_add_comp_17_s3_msb), .pb0(hamming_add_comp_17_pb0), .pb1(hamming_add_comp_17_pb1),
    .RST(RSET), .b0_2(n8bit_reg_s2_4_b0_2), .b1_2(n8bit_reg_s2_4_b1_2), .b2_2(n8bit_reg_s2_4_b2_2),
    .b3_2(n8bit_reg_s2_4_b3_2), .pb0_2(C5R3_0), .pb1_2(C5R3_1), .sb0(n8bit_reg_s2_4_sb0),
    .sb1(n8bit_reg_s2_4_sb1));
  _8bit_reg_S3 u_8bit_reg_s3_4 (
    .clk(CLK), .b0(hamming_add_comp_18_s0_lsb), .b1(hamming_add_comp_18_s1), .b2(hamming_add_comp_18_s2),
    .b3(hamming_add_comp_18_s3_msb), .pb0(hamming_add_comp_18_pb0), .pb1(hamming_add_comp_18_pb1),
    .RST(RSET), .b0_2(n8bit_reg_s3_4_b0_2), .b1_2(n8bit_reg_s3_4_b1_2), .b2_2(n8bit_reg_s3_4_b2_2),
    .b3_2(n8bit_reg_s3_4_b3_2), .pb0_2(C5R4_0), .pb1_2(C5R4_1), .sb0(n8bit_reg_s3_4_sb0),
    .sb1(n8bit_reg_s3_4_sb1));
  hamming_add_comp hamming_add_comp_19 (
    .EXT(1'b0), .B01(n8bit_reg_s0_6_b2_2), .B02(n8bit_reg_s0_6_b3_2), .B03(C5R1_0), .CIN0(C0), .IN00(1'b0),
    .CIN1(C1), .IN01(1'b0), .B10(n8bit_reg_s2_4_b0_2), .B11(n8bit_reg_s2_4_b1_2), .B12(n8bit_reg_s2_4_b2_2),
    .B13(n8bit_reg_s2_4_b3_2), .IN10(1'b1), .IN11(1'b1), .AS0(n8bit_reg_s0_6_sb0), .AS1(n8bit_reg_s0_6_sb1),
    .BS0(n8bit_reg_s2_4_sb0), .BS1(n8bit_reg_s2_4_sb1), .B00(n8bit_reg_s0_6_b1_2),
    .S0_lsb(hamming_add_comp_19_s0_lsb), .S1(hamming_add_comp_19_s1), .S2(hamming_add_comp_19_s2),
    .S3_msb(hamming_add_comp_19_s3_msb), .PB0(hamming_add_comp_19_pb0), .PB1(hamming_add_comp_19_pb1));
  hamming_add_comp hamming_add_comp_20 (
    .EXT(1'b0), .B01(n8bit_reg_s0_6_b2_2), .B02(n8bit_reg_s0_6_b3_2), .B03(C5R1_0), .CIN0(C0), .IN00(1'b1),
    .CIN1(C1), .IN01(1'b1), .B10(n8bit_reg_s2_4_b0_2), .B11(n8bit_reg_s2_4_b1_2), .B12(n8bit_reg_s2_4_b2_2),
    .B13(n8bit_reg_s2_4_b3_2), .IN10(1'b0), .IN11(1'b0), .AS0(n8bit_reg_s0_6_sb0), .AS1(n8bit_reg_s0_6_sb1),
    .BS0(n8bit_reg_s2_4_sb0), .BS1(n8bit_reg_s2_4_sb1), .B00(n8bit_reg_s0_6_b1_2),
    .S0_lsb(hamming_add_comp_20_s0_lsb), .S1(hamming_add_comp_20_s1), .S2(hamming_add_comp_20_s2),
    .S3_msb(hamming_add_comp_20_s3_msb), .PB0(hamming_add_comp_20_pb0), .PB1(hamming_add_comp_20_pb1));
  hamming_add_comp hamming_add_comp_21 (
    .EXT(1'b0), .B01(n8bit_reg_s1_5_b1_2), .B02(n8bit_reg_s1_5_b2_2), .B03(n8bit_reg_s1_5_b3_2), .CIN0(C0),
    .IN00(1'b1), .CIN1(C1), .IN01(1'b0), .B10(n8bit_reg_s3_4_b0_2), .B11(n8bit_reg_s3_4_b1_2),
    .B12(n8bit_reg_s3_4_b2_2), .B13(n8bit_reg_s3_4_b3_2), .IN10(1'b0), .IN11(1'b1), .AS0(n8bit_reg_s1_5_sb0),
    .AS1(n8bit_reg_s1_5_sb1), .BS0(n8bit_reg_s3_4_sb0), .BS1(n8bit_reg_s3_4_sb1), .B00(n8bit_reg_s1_5_b0_2),
    .S0_lsb(hamming_add_comp_21_s0_lsb), .S1(hamming_add_comp_21_s1), .S2(hamming_add_comp_21_s2),
    .S3_msb(hamming_add_comp_21_s3_msb), .PB0(hamming_add_comp_21_pb0), .PB1(hamming_add_comp_21_pb1));
  hamming_add_comp hamming_add_comp_22 (
    .EXT(1'b0), .B01(n8bit_reg_s1_5_b1_2), .B02(n8bit_reg_s1_5_b2_2), .B03(n8bit_reg_s1_5_b3_2), .CIN0(C0),
    .IN00(1'b0), .CIN1(C1), .IN01(1'b1), .B10(n8bit_reg_s3_4_b0_2), .B11(n8bit_reg_s3_4_b1_2),
    .B12(n8bit_reg_s3_4_b2_2), .B13(n8bit_reg_s3_4_b3_2), .IN10(1'b1), .IN11(1'b0), .AS0(n8bit_reg_s1_5_sb0),
    .AS1(n8bit_reg_s1_5_sb1), .BS0(n8bit_reg_s3_4_sb0), .BS1(n8bit_reg_s3_4_sb1), .B00(n8bit_reg_s1_5_b0_2),
    .S0_lsb(hamming_add_comp_22_s0_lsb), .S1(hamming_add_comp_22_s1), .S2(hamming_add_comp_22_s2),
    .S3_msb(hamming_add_comp_22_s3_msb), .PB0(hamming_add_comp_22_pb0), .PB1(hamming_add_comp_22_pb1));
  _8bit_reg_S0 u_8bit_reg_s0_7 (
    .clk(CLK), .b0(hamming_add_comp_19_s0_lsb), .b1(hamming_add_comp_19_s1), .b2(hamming_add_comp_19_s2),
    .b3(hamming_add_comp_19_s3_msb), .pb0(hamming_add_comp_19_pb0), .pb1(hamming_add_comp_19_pb1),
    .RST(RSET), .b0_2(n8bit_reg_s0_7_b0_2), .b1_2(n8bit_reg_s0_7_b1_2), .b2_2(n8bit_reg_s0_7_b2_2),
    .b3_2(n8bit_reg_s0_7_b3_2), .pb0_2(n8bit_reg_s0_7_pb0_2), .pb1_2(n8bit_reg_s0_7_pb1_2));  // open: sb0, sb1
  _8bit_reg_S1 u_8bit_reg_s1_6 (
    .clk(CLK), .b0(hamming_add_comp_20_s0_lsb), .b1(hamming_add_comp_20_s1), .b2(hamming_add_comp_20_s2),
    .b3(hamming_add_comp_20_s3_msb), .pb0(hamming_add_comp_20_pb0), .pb1(hamming_add_comp_20_pb1),
    .RST(RSET), .b0_2(n8bit_reg_s1_6_b0_2), .b1_2(n8bit_reg_s1_6_b1_2), .b2_2(n8bit_reg_s1_6_b2_2),
    .b3_2(n8bit_reg_s1_6_b3_2), .pb0_2(n8bit_reg_s1_6_pb0_2), .pb1_2(n8bit_reg_s1_6_pb1_2));  // open: sb0, sb1
  _8bit_reg_S2 u_8bit_reg_s2_5 (
    .clk(CLK), .b0(hamming_add_comp_21_s0_lsb), .b1(hamming_add_comp_21_s1), .b2(hamming_add_comp_21_s2),
    .b3(hamming_add_comp_21_s3_msb), .pb0(hamming_add_comp_21_pb0), .pb1(hamming_add_comp_21_pb1),
    .RST(RSET), .b0_2(n8bit_reg_s2_5_b0_2), .b1_2(n8bit_reg_s2_5_b1_2), .b2_2(n8bit_reg_s2_5_b2_2),
    .b3_2(n8bit_reg_s2_5_b3_2), .pb0_2(n8bit_reg_s2_5_pb0_2), .pb1_2(n8bit_reg_s2_5_pb1_2));  // open: sb0, sb1
  _8bit_reg_S3 u_8bit_reg_s3_5 (
    .clk(CLK), .b0(hamming_add_comp_22_s0_lsb), .b1(hamming_add_comp_22_s1), .b2(hamming_add_comp_22_s2),
    .b3(hamming_add_comp_22_s3_msb), .pb0(hamming_add_comp_22_pb0), .pb1(hamming_add_comp_22_pb1),
    .RST(RSET), .b0_2(n8bit_reg_s3_5_b0_2), .b1_2(n8bit_reg_s3_5_b1_2), .b2_2(n8bit_reg_s3_5_b2_2),
    .b3_2(n8bit_reg_s3_5_b3_2), .pb0_2(n8bit_reg_s3_5_pb0_2), .pb1_2(n8bit_reg_s3_5_pb1_2));  // open: sb0, sb1
  mag4_comp_main main_1 (
    .A3(n8bit_reg_s0_7_b3_2), .A2(n8bit_reg_s0_7_b2_2), .A1(n8bit_reg_s0_7_b1_2), .A0(n8bit_reg_s0_7_b0_2),
    .B3(n8bit_reg_s1_6_b3_2), .B2(n8bit_reg_s1_6_b2_2), .B1(n8bit_reg_s1_6_b1_2), .B0(n8bit_reg_s1_6_b0_2),
    .A_B(main_1_a_b), .A_B_3(main_1_a_b_3));  // open: A_B_2
  or or_1 (or_1_out, main_1_a_b, main_1_a_b_3);
  Multiplexer multiplexer_1 (
    .in0(n8bit_reg_s0_7_b3_2), .in1(n8bit_reg_s1_6_b3_2), .out(multiplexer_1_out), .sel(or_1_out));  // open: en
  Multiplexer multiplexer_2 (
    .in0(n8bit_reg_s0_7_b2_2), .in1(n8bit_reg_s1_6_b2_2), .out(multiplexer_2_out), .sel(or_1_out));  // open: en
  Multiplexer multiplexer_3 (
    .in0(n8bit_reg_s0_7_b1_2), .in1(n8bit_reg_s1_6_b1_2), .out(multiplexer_3_out), .sel(or_1_out));  // open: en
  Multiplexer multiplexer_4 (
    .in0(n8bit_reg_s0_7_b0_2), .in1(n8bit_reg_s1_6_b0_2), .out(multiplexer_4_out), .sel(or_1_out));  // open: en
  mag4_comp_main main_2 (
    .A3(n8bit_reg_s2_5_b3_2), .A2(n8bit_reg_s2_5_b2_2), .A1(n8bit_reg_s2_5_b1_2), .A0(n8bit_reg_s2_5_b0_2),
    .B3(n8bit_reg_s3_5_b3_2), .B2(n8bit_reg_s3_5_b2_2), .B1(n8bit_reg_s3_5_b1_2), .B0(n8bit_reg_s3_5_b0_2),
    .A_B(main_2_a_b), .A_B_3(main_2_a_b_3));  // open: A_B_2
  Multiplexer multiplexer_5 (
    .in0(n8bit_reg_s0_7_pb1_2), .in1(n8bit_reg_s1_6_pb1_2), .out(multiplexer_5_out), .sel(or_1_out));  // open: en
  Multiplexer multiplexer_6 (
    .in0(n8bit_reg_s0_7_pb0_2), .in1(n8bit_reg_s1_6_pb0_2), .out(multiplexer_6_out), .sel(or_1_out));  // open: en
  or or_2 (or_2_out, main_2_a_b, main_2_a_b_3);
  Multiplexer multiplexer_7 (
    .in0(n8bit_reg_s2_5_pb1_2), .in1(n8bit_reg_s3_5_pb1_2), .out(multiplexer_7_out), .sel(or_2_out));  // open: en
  Multiplexer multiplexer_8 (
    .in0(n8bit_reg_s2_5_pb0_2), .in1(n8bit_reg_s3_5_pb0_2), .out(multiplexer_8_out), .sel(or_2_out));  // open: en
  Multiplexer multiplexer_9 (
    .in0(n8bit_reg_s2_5_b3_2), .in1(n8bit_reg_s3_5_b3_2), .out(multiplexer_9_out), .sel(or_2_out));  // open: en
  Multiplexer multiplexer_10 (
    .in0(n8bit_reg_s2_5_b2_2), .in1(n8bit_reg_s3_5_b2_2), .out(multiplexer_10_out), .sel(or_2_out));  // open: en
  Multiplexer multiplexer_11 (
    .in0(n8bit_reg_s2_5_b1_2), .in1(n8bit_reg_s3_5_b1_2), .out(multiplexer_11_out), .sel(or_2_out));  // open: en
  Multiplexer multiplexer_12 (
    .in0(n8bit_reg_s2_5_b0_2), .in1(n8bit_reg_s3_5_b0_2), .out(multiplexer_12_out), .sel(or_2_out));  // open: en
  mag4_comp_main main_3 (
    .A3(multiplexer_1_out), .A2(multiplexer_2_out), .A1(multiplexer_3_out), .A0(multiplexer_4_out),
    .B3(multiplexer_9_out), .B2(multiplexer_10_out), .B1(multiplexer_11_out), .B0(multiplexer_12_out),
    .A_B(main_3_a_b), .A_B_3(main_3_a_b_3));  // open: A_B_2
  or or_3 (or_3_out, main_3_a_b, main_3_a_b_3);
  Multiplexer multiplexer_13 (.in0(multiplexer_5_out), .in1(multiplexer_7_out), .out(L1), .sel(or_3_out));  // open: en
  Multiplexer multiplexer_14 (.in0(multiplexer_6_out), .in1(multiplexer_8_out), .out(L0), .sel(or_3_out));  // open: en

  // Notes on the sheet:
  //   required liraries:
  //   shift_reg,4stages
  //   hammin+adder+comp
  //   4bit_comparator
endmodule
